// Digital circuit 2a5-bcd.dig as structural Verilog
module _2a5_bcd (
  input  I3,
  input  I2,
  input  I1,
  input  I0,
  output X
);

  wire or_1_out;

  or or_1 (or_1_out, I2, I1);
  and and_1 (X, I3, or_1_out);

  // Notes on the sheet:
  //   RTC
  //   Switches
  //   7
  //   6
  //   5
  //   4
  //   3
  //   2
  //   1
  //   0
  //   Pulsers
  //   L
  //   R
  //   LEDs
  //   Hex Display
endmodule
