// Digital circuit 2c2-decoder.dig as structural Verilog
module _2c2_decoder (
  input  [2:0] S,
  output Y_0,
  output Y_4,
  output Y_6,
  output Y_5,
  output Y_3,
  output Y_1,
  output Y_2,
  output Y_7
);

  Decoder #(.Selector_Bits(3)) decoder_1 (
    .sel(S), .out_0(Y_0), .out_1(Y_1), .out_2(Y_2), .out_3(Y_3), .out_4(Y_4), .out_5(Y_5), .out_6(Y_6),
    .out_7(Y_7));

  // Notes on the sheet:
  //   RTC
  //   Switches
  //   7
  //   6
  //   5
  //   4
  //   3
  //   2
  //   1
  //   0
  //   Pulsers
  //   L
  //   R
  //   LEDs
  //   Hex Display
endmodule
