// Digital circuit 2d1-mux.dig as structural Verilog
module _2d1_mux (
  input  A,
  input  B,
  input  C,
  input  D,
  output X
);

  wire _7404_1_pin8;

  _7404 _7404_1 (
    .pin1(1'b0), .pin3(1'b0), .pin5(1'b0), .pin7(1'b0), .pin8(_7404_1_pin8), .pin9(D), .pin11(1'b0),
    .pin13(1'b0), .pin14(1'b1));  // open: pin2, pin4, pin6, pin10, pin12
  _74151 _74151_1 (
    .pin1(D), .pin2(_7404_1_pin8), .pin3(1'b0), .pin4(D), .pin5(X), .pin7(1'b0), .pin8(1'b0), .pin9(A),
    .pin10(B), .pin11(C), .pin12(_7404_1_pin8), .pin13(D), .pin14(1'b0), .pin15(1'b1), .pin16(1'b1));  // open: pin6

  // Notes on the sheet:
  //   RTC
  //   Switches
  //   7
  //   6
  //   5
  //   4
  //   3
  //   2
  //   1
  //   0
  //   Pulsers
  //   L
  //   R
  //   LEDs
  //   Hex Display
endmodule
