// Digital circuit 2d2-mysterious-circuit.dig as structural Verilog
module _2d2_mysterious_circuit (
  input  B_3,
  input  B_2,
  input  B_1,
  input  B_0,
  output G_3,
  output G_2,
  output G_1,
  output G_0
);

  xor xor_1 (G_2, B_2, B_3);
  xor xor_2 (G_1, B_1, B_2);
  xor xor_3 (G_0, B_0, B_1);

  assign G_3 = B_3;
endmodule
