// Digital circuit 3a1-basic-sr-latch.dig as structural Verilog
module _3a1_basic_sr_latch (
  input  in_1,
  output out_2,
  output out_3
);

  nand nand_1 (out_2, in_1, out_3);
  nand nand_2 (out_3, out_2, in_1);
endmodule
