// Digital circuit 3a2-sr-latch-with-enable.dig as structural Verilog
module _3a2_sr_latch_with_enable (
  input  in_1,
  input  in_2,
  output out_3,
  output out_4
);

  wire nand_1_out, nand_2_out;

  nand nand_1 (nand_1_out, in_1, in_2);
  nand nand_2 (nand_2_out, in_2, in_1);
  nand nand_3 (out_3, nand_1_out, out_4);
  nand nand_4 (out_4, out_3, nand_2_out);
endmodule
