// Digital circuit 3a3-transparent-latch-with-enable.dig as structural Verilog
module _3a3_transparent_latch_with_enable (
  input  in_1,
  output out_2,
  output out_3
);

  wire nand_1_out, nand_2_out, not_1_out;

  not not_1 (not_1_out, in_1);
  nand nand_1 (nand_1_out, in_1, in_1);
  nand nand_2 (nand_2_out, in_1, not_1_out);
  nand nand_3 (out_2, nand_1_out, out_3);
  nand nand_4 (out_3, out_2, nand_2_out);
endmodule
