// Digital circuit 3a4-d-flip-flop-component.dig as structural Verilog
module _3a4_d_flip_flop_component (
  input  PRE,
  input  D,
  input  RST,
  output Q
);

  wire CLK_out;

  Button CLK (.out(CLK_out));
  D_FF_AS d_ff_as_1 (.Set(~PRE), .D(D), .C(CLK_out), .Clr(~RST), .Q(Q));  // open: nQ
endmodule
