// Digital circuit 3a5-tff.dig as structural Verilog
module _3a5_tff (
  input  T,
  input  PRE,
  input  RST,
  output Q
);

  wire _7486_1_pin8, CLK_out;

  _7486 _7486_1 (
    .pin1(1'b0), .pin2(1'b0), .pin3(1'b0), .pin4(1'b0), .pin5(1'b0), .pin6(1'b0), .pin7(1'b0),
    .pin8(_7486_1_pin8), .pin9(Q), .pin10(T), .pin11(1'b0), .pin12(1'b0), .pin13(1'b0), .pin14(1'b1));
  Button CLK (.out(CLK_out));
  _7474 _7474_1 (
    .pin1(1'b0), .pin2(1'b0), .pin3(1'b0), .pin4(1'b0), .pin7(1'b0), .pin9(Q), .pin10(PRE), .pin11(CLK_out),
    .pin12(_7486_1_pin8), .pin13(RST), .pin14(1'b1));  // open: pin5, pin6, pin8

  // Notes on the sheet:
  //   RTC
  //   Switches
  //   7
  //   6
  //   5
  //   4
  //   3
  //   2
  //   1
  //   0
  //   Pulsers
  //   L
  //   R
  //   LEDs
  //   Hex Display
endmodule
