// Digital circuit 3c2.dig as structural Verilog
module _3c2 (
  input  CLK,
  output Z,
  output QA,
  output nQB,
  output QB,
  output nQB_2
);

  wire PRE_A_out, PRE_B_out, RST_A_out, RST_B_out;

  xnor xnor_1 (Z, QB, QA);
  Button PRE_A (.out(PRE_A_out));
  Button RST_A (.out(RST_A_out));
  Button PRE_B (.out(PRE_B_out));
  Button RST_B (.out(RST_B_out));
  JK_FF_AS FF_A (.Set(PRE_A_out), .J(QA), .C(CLK), .K(nQB), .Clr(RST_A_out), .Q(QA), .nQ(nQB));
  JK_FF_AS FF_B (.Set(PRE_B_out), .J(QB), .C(CLK), .K(nQB_2), .Clr(RST_B_out), .Q(QB), .nQ(nQB_2));

  // Other names for the same wires on the sheet: nQ_A = nQB_2; nQ_B = nQB; Q_A = QB; Q_B = QA
endmodule
