// Digital circuit 3d4.dig as structural Verilog
module _3d4 (
  input  clk
);

  wire and_1_out, and_2_out, and_3_out, and_4_out, nQ0, nQ1, nQ2, or_1_out, or_2_out, Q0, Q1, Q2;

  and and_1 (and_1_out, nQ2, nQ1, nQ0);
  and and_2 (and_2_out, Q2, nQ1, nQ0);
  and and_3 (and_3_out, nQ2, Q1, Q0);
  or or_1 (or_1_out, Q2, Q1);
  D_FF D2 (.D(and_1_out), .C(clk), .Q(Q2), .nQ(nQ2));
  or or_2 (or_2_out, and_2_out, and_3_out);
  and and_4 (and_4_out, or_1_out, nQ0);
  D_FF D1 (.D(or_2_out), .C(clk), .Q(Q1), .nQ(nQ1));
  D_FF D0 (.D(and_4_out), .C(clk), .Q(Q0), .nQ(nQ0));
  LED u_Q2 (.in(Q2));
  LED u_Q1 (.in(Q1));
  LED u_Q0 (.in(Q0));
endmodule
