// Digital circuit digichip-example-build.dig as structural Verilog
module digichip_example_build (
  input  A3,
  input  A2,
  input  A1,
  input  A0,
  input  B3,
  input  B2,
  input  B1,
  input  B0,
  output pin5,
  output pin6,
  output pin7
);

  _7485 _7485_1 (
    .pin1(B3), .pin2(1'b0), .pin3(1'b1), .pin4(1'b0), .pin5(pin5), .pin6(pin6), .pin7(pin7), .pin8(1'b0),
    .pin9(B0), .pin10(A0), .pin11(B1), .pin12(A1), .pin13(A2), .pin14(B2), .pin15(A3), .pin16(1'b1));

  // Notes on the sheet:
  //   RTC
  //   Switches
  //   7
  //   6
  //   5
  //   4
  //   3
  //   2
  //   1
  //   0
  //   Pulsers
  //   L
  //   R
  //   LEDs
  //   Hex Display
endmodule
