// Digital circuit trainer-simple.dig as structural Verilog
module trainer_simple (
  input  in_1,
  input  in_2,
  input  in_3,
  input  in_4,
  input  in_5,
  input  in_6,
  input  in_7,
  input  in_8,
  input  clk,
  output out_9,
  output out_10,
  output out_11,
  output out_12,
  output out_13,
  output out_14,
  output out_15,
  output out_16
);

  wire [3:0] undriven;

  Button button_1 ();  // open: out
  Button button_2 ();  // open: out
  Seven_Seg_Hex seven_seg_hex_1 (.d(undriven), .dp(1'b0));

  // Notes on the sheet:
  //   RTC
  //   Switches
  //   7
  //   6
  //   5
  //   4
  //   3
  //   2
  //   1
  //   0
  //   Pulsers
  //   L
  //   R
  //   LEDs
  //   Hex Display
  //   X
endmodule
